// Logisim project RelogioDigitalAMPM.circ as structural Verilog: 4 circuits, main circuit main
module main (
);

  wire and_1_out, and_2_out, and_3_out, and_4_out, and_5_out, and_6_out, aup_1_out_2, aup_1_out_3,
       aup_1_out_4, aup_1_out_5, aup_1_out_6, aup_1_out_7, aup_1_out_8, clock_1_out, decodificador2_1_b,
       decodificador2_1_b_2, decodificador2_1_b_3, decodificador2_1_b_4, decodificador2_1_out_9,
       decodificador2_1_out_10, decodificador2_1_out_11, decodificador2_1_out_12, decodificador_1_a_2,
       decodificador_1_b_2, decodificador_1_c_2, decodificador_1_d_2, decodificador_1_e, decodificador_1_f,
       decodificador_1_g, decodificador_2_a_2, decodificador_2_b_2, decodificador_2_c_2, decodificador_2_d_2,
       decodificador_2_e, decodificador_2_f, decodificador_2_g, decodificador_3_a_2, decodificador_3_b_2,
       decodificador_3_c_2, decodificador_3_d_2, decodificador_3_e, decodificador_3_f, decodificador_3_g,
       decodificador_4_a_2, decodificador_4_b_2, decodificador_4_c_2, decodificador_4_d_2, decodificador_4_e,
       decodificador_4_f, decodificador_4_g, decodificador_5_a_2, decodificador_5_b_2, decodificador_5_c_2,
       decodificador_5_d_2, decodificador_5_e, decodificador_5_f, decodificador_5_g, decodificador_6_a_2,
       decodificador_6_b_2, decodificador_6_c_2, decodificador_6_d_2, decodificador_6_e, decodificador_6_f,
       decodificador_6_g, j_k_ff_1_q, j_k_ff_2_q, j_k_ff_3_q, j_k_ff_4_q, j_k_ff_5_q, j_k_ff_6_q, j_k_ff_7_q,
       j_k_ff_8_q, j_k_ff_9_q, j_k_ff_10_q, j_k_ff_11_q, j_k_ff_12_q, j_k_ff_13_q, j_k_ff_14_q, j_k_ff_15_q,
       j_k_ff_16_q, j_k_ff_17_q, j_k_ff_18_q, j_k_ff_19_q, j_k_ff_20_q, j_k_ff_21_q, j_k_ff_22_q, or_1_out;

  Clock clock_1 (.out(clock_1_out));
  J_K_Flip_Flop #(.trigger("falling")) j_k_ff_1 (
    .J(1'b1), .clk(clock_1_out), .K(1'b1), .Q(j_k_ff_1_q), .reset(and_3_out));  // open: Qn, preset, en
  J_K_Flip_Flop #(.trigger("falling")) j_k_ff_2 (
    .J(1'b1), .clk(and_3_out), .K(1'b1), .Q(j_k_ff_2_q), .reset(and_1_out));  // open: Qn, preset, en
  J_K_Flip_Flop #(.trigger("falling")) j_k_ff_3 (
    .J(1'b1), .clk(and_1_out), .K(1'b1), .Q(j_k_ff_3_q), .reset(and_4_out));  // open: Qn, preset, en
  J_K_Flip_Flop #(.trigger("falling")) j_k_ff_4 (
    .J(1'b1), .clk(and_4_out), .K(1'b1), .Q(j_k_ff_4_q), .reset(and_2_out));  // open: Qn, preset, en
  J_K_Flip_Flop #(.trigger("falling")) j_k_ff_5 (
    .J(1'b1), .clk(and_2_out), .K(1'b1), .Q(j_k_ff_5_q), .reset(or_1_out));  // open: Qn, preset, en
  J_K_Flip_Flop #(.trigger("falling")) j_k_ff_6 (
    .J(1'b1), .clk(or_1_out), .K(1'b1), .Q(j_k_ff_6_q), .reset(j_k_ff_11_q));  // open: Qn, preset, en
  J_K_Flip_Flop #(.trigger("falling")) j_k_ff_7 (
    .J(1'b1), .clk(j_k_ff_1_q), .K(1'b1), .Q(j_k_ff_7_q), .reset(and_3_out));  // open: Qn, preset, en
  J_K_Flip_Flop #(.trigger("falling")) j_k_ff_8 (
    .J(1'b1), .clk(j_k_ff_2_q), .K(1'b1), .Q(j_k_ff_8_q), .reset(and_1_out));  // open: Qn, preset, en
  J_K_Flip_Flop #(.trigger("falling")) j_k_ff_9 (
    .J(1'b1), .clk(j_k_ff_3_q), .K(1'b1), .Q(j_k_ff_9_q), .reset(and_4_out));  // open: Qn, preset, en
  J_K_Flip_Flop #(.trigger("falling")) j_k_ff_10 (
    .J(1'b1), .clk(j_k_ff_4_q), .K(1'b1), .Q(j_k_ff_10_q), .reset(and_2_out));  // open: Qn, preset, en
  J_K_Flip_Flop #(.trigger("falling")) j_k_ff_11 (
    .J(1'b1), .clk(j_k_ff_6_q), .K(1'b1), .Q(j_k_ff_11_q), .reset(j_k_ff_11_q));  // open: Qn, preset, en
  J_K_Flip_Flop #(.trigger("falling")) j_k_ff_12 (
    .J(1'b1), .clk(j_k_ff_6_q), .K(1'b1), .Q(j_k_ff_12_q), .reset(j_k_ff_15_q));  // open: Qn, preset, en
  J_K_Flip_Flop #(.trigger("falling")) j_k_ff_13 (
    .J(1'b1), .clk(j_k_ff_7_q), .K(1'b1), .Q(j_k_ff_13_q), .reset(and_3_out));  // open: Qn, preset, en
  J_K_Flip_Flop #(.trigger("falling")) j_k_ff_14 (
    .J(1'b1), .clk(j_k_ff_5_q), .K(1'b1), .Q(j_k_ff_14_q), .reset(or_1_out));  // open: Qn, preset, en
  J_K_Flip_Flop #(.trigger("falling")) j_k_ff_15 (
    .J(1'b1), .clk(j_k_ff_12_q), .K(1'b1), .Q(j_k_ff_15_q), .reset(j_k_ff_15_q));  // open: Qn, preset, en
  J_K_Flip_Flop #(.trigger("falling")) j_k_ff_16 (
    .J(1'b1), .clk(j_k_ff_8_q), .K(1'b1), .Q(j_k_ff_16_q), .reset(and_1_out));  // open: Qn, preset, en
  and and_1 (and_1_out, j_k_ff_16_q, j_k_ff_8_q);
  J_K_Flip_Flop #(.trigger("falling")) j_k_ff_17 (
    .J(1'b1), .clk(j_k_ff_9_q), .K(1'b1), .Q(j_k_ff_17_q), .reset(and_4_out));  // open: Qn, preset, en
  J_K_Flip_Flop #(.trigger("falling")) j_k_ff_18 (
    .J(1'b1), .clk(j_k_ff_10_q), .K(1'b1), .Q(j_k_ff_18_q), .reset(and_2_out));  // open: Qn, preset, en
  and and_2 (and_2_out, j_k_ff_18_q, j_k_ff_10_q);
  J_K_Flip_Flop #(.trigger("falling")) j_k_ff_19 (
    .J(1'b1), .clk(j_k_ff_14_q), .K(1'b1), .Q(j_k_ff_19_q), .reset(or_1_out));  // open: Qn, preset, en
  J_K_Flip_Flop #(.trigger("falling")) j_k_ff_20 (
    .J(1'b1), .clk(j_k_ff_13_q), .K(1'b1), .Q(j_k_ff_20_q), .reset(and_3_out));  // open: Qn, preset, en
  and and_3 (and_3_out, j_k_ff_20_q, j_k_ff_7_q);
  J_K_Flip_Flop #(.trigger("falling")) j_k_ff_21 (
    .J(1'b1), .clk(j_k_ff_17_q), .K(1'b1), .Q(j_k_ff_21_q), .reset(and_4_out));  // open: Qn, preset, en
  and and_4 (and_4_out, j_k_ff_21_q, j_k_ff_9_q);
  J_K_Flip_Flop #(.trigger("falling")) j_k_ff_22 (
    .J(1'b1), .clk(j_k_ff_19_q), .K(1'b1), .Q(j_k_ff_22_q), .reset(or_1_out));  // open: Qn, preset, en
  or or_1 (or_1_out, and_6_out, and_5_out);
  and and_5 (and_5_out, j_k_ff_14_q, j_k_ff_6_q);
  and and_6 (and_6_out, j_k_ff_22_q, j_k_ff_14_q);
  _7_Segment_Display u_7_segment_display_1 (
    .g(decodificador_1_g), .f(decodificador_1_f), .a(decodificador_1_a_2), .b(decodificador_1_b_2),
    .e(decodificador_1_e), .d(decodificador_1_d_2), .c(decodificador_1_c_2));  // open: dp
  Decodificador decodificador_1 (
    .A(decodificador2_1_out_9), .B(decodificador2_1_out_10), .C(decodificador2_1_out_11),
    .D(decodificador2_1_out_12), .g(decodificador_1_g), .f(decodificador_1_f), .a_2(decodificador_1_a_2),
    .b_2(decodificador_1_b_2), .c_2(decodificador_1_c_2), .d_2(decodificador_1_d_2), .e(decodificador_1_e));
  _7_Segment_Display u_7_segment_display_2 (
    .g(decodificador_2_g), .f(decodificador_2_f), .a(decodificador_2_a_2), .b(decodificador_2_b_2),
    .e(decodificador_2_e), .d(decodificador_2_d_2), .c(decodificador_2_c_2));  // open: dp
  Decodificador2 decodificador2_1 (
    ._0(j_k_ff_6_q), ._1(1'b0), ._2(1'b0), ._3(1'b0), .out_9(decodificador2_1_out_9),
    .out_10(decodificador2_1_out_10), .out_11(decodificador2_1_out_11), .out_12(decodificador2_1_out_12),
    .b(decodificador2_1_b), .b_2(decodificador2_1_b_2), .b_3(decodificador2_1_b_3),
    .b_4(decodificador2_1_b_4), ._0_2(j_k_ff_22_q), ._1_2(j_k_ff_19_q), ._2_2(j_k_ff_14_q), ._3_2(j_k_ff_5_q));
  Decodificador decodificador_2 (
    .A(decodificador2_1_b), .B(decodificador2_1_b_2), .C(decodificador2_1_b_3), .D(decodificador2_1_b_4),
    .g(decodificador_2_g), .f(decodificador_2_f), .a_2(decodificador_2_a_2), .b_2(decodificador_2_b_2),
    .c_2(decodificador_2_c_2), .d_2(decodificador_2_d_2), .e(decodificador_2_e));
  _7_Segment_Display u_7_segment_display_3 (
    .g(decodificador_3_g), .f(decodificador_3_f), .a(decodificador_3_a_2), .b(decodificador_3_b_2),
    .e(decodificador_3_e), .d(decodificador_3_d_2), .c(decodificador_3_c_2));  // open: dp
  LED led_1 (.in(1'b1));
  LED led_2 (.in(1'b1));
  Decodificador decodificador_3 (
    .A(1'b0), .B(j_k_ff_18_q), .C(j_k_ff_10_q), .D(j_k_ff_4_q), .g(decodificador_3_g), .f(decodificador_3_f),
    .a_2(decodificador_3_a_2), .b_2(decodificador_3_b_2), .c_2(decodificador_3_c_2),
    .d_2(decodificador_3_d_2), .e(decodificador_3_e));
  _7_Segment_Display u_7_segment_display_4 (
    .g(decodificador_4_g), .f(decodificador_4_f), .a(decodificador_4_a_2), .b(decodificador_4_b_2),
    .e(decodificador_4_e), .d(decodificador_4_d_2), .c(decodificador_4_c_2));  // open: dp
  Decodificador decodificador_4 (
    .A(j_k_ff_21_q), .B(j_k_ff_17_q), .C(j_k_ff_9_q), .D(j_k_ff_3_q), .g(decodificador_4_g),
    .f(decodificador_4_f), .a_2(decodificador_4_a_2), .b_2(decodificador_4_b_2), .c_2(decodificador_4_c_2),
    .d_2(decodificador_4_d_2), .e(decodificador_4_e));
  LED led_3 (.in(1'b1));
  LED led_4 (.in(1'b1));
  Decodificador decodificador_5 (
    .A(1'b0), .B(j_k_ff_16_q), .C(j_k_ff_8_q), .D(j_k_ff_2_q), .g(decodificador_5_g), .f(decodificador_5_f),
    .a_2(decodificador_5_a_2), .b_2(decodificador_5_b_2), .c_2(decodificador_5_c_2),
    .d_2(decodificador_5_d_2), .e(decodificador_5_e));
  _7_Segment_Display u_7_segment_display_5 (
    .g(decodificador_5_g), .f(decodificador_5_f), .a(decodificador_5_a_2), .b(decodificador_5_b_2),
    .e(decodificador_5_e), .d(decodificador_5_d_2), .c(decodificador_5_c_2));  // open: dp
  Decodificador decodificador_6 (
    .A(j_k_ff_20_q), .B(j_k_ff_13_q), .C(j_k_ff_7_q), .D(j_k_ff_1_q), .g(decodificador_6_g),
    .f(decodificador_6_f), .a_2(decodificador_6_a_2), .b_2(decodificador_6_b_2), .c_2(decodificador_6_c_2),
    .d_2(decodificador_6_d_2), .e(decodificador_6_e));
  _7_Segment_Display u_7_segment_display_6 (
    .g(decodificador_6_g), .f(decodificador_6_f), .a(decodificador_6_a_2), .b(decodificador_6_b_2),
    .e(decodificador_6_e), .d(decodificador_6_d_2), .c(decodificador_6_c_2));  // open: dp
  AUP aup_1 (
    .in_1(j_k_ff_12_q), .out_2(aup_1_out_2), .out_3(aup_1_out_3), .out_4(aup_1_out_4), .out_5(aup_1_out_5),
    .out_6(aup_1_out_6), .out_7(aup_1_out_7), .out_8(aup_1_out_8));
  _7_Segment_Display u_7_segment_display_7 (
    .g(aup_1_out_2), .f(aup_1_out_3), .a(aup_1_out_4), .b(aup_1_out_5), .e(aup_1_out_6), .d(aup_1_out_7),
    .c(aup_1_out_8));  // open: dp
  _7_Segment_Display u_7_segment_display_8 (.g(1'b1), .a(1'b1), .e(1'b1), .c(1'b1));  // open: f, b, d, dp

  // Notes on the sheet:
  //   A & P
  //   HORAS
  //   MINUTOS
  //   SEGUNDOS
endmodule

module Decodificador (
  input  A,
  input  B,
  input  C,
  input  D,
  output c_2,
  output d_2,
  output e,
  output g,
  output f,
  output a_2,
  output b_2
);

  wire and_1_out, and_2_out, and_3_out, and_4_out, and_5_out, and_6_out, and_7_out, and_8_out, and_9_out,
       and_10_out, and_11_out, and_12_out, and_13_out, and_14_out, and_15_out, and_16_out, not_1_out,
       not_2_out, not_3_out;

  not not_1 (not_1_out, B);
  not not_2 (not_2_out, C);
  not not_3 (not_3_out, D);
  and and_1 (and_1_out, B, D);
  and and_2 (and_2_out, not_1_out, not_3_out);
  and and_3 (and_3_out, C, D);
  and and_4 (and_4_out, not_2_out, not_3_out);
  and and_5 (and_5_out, not_1_out, not_3_out);
  and and_6 (and_6_out, not_1_out, C);
  and and_7 (and_7_out, C, not_3_out);
  and and_8 (and_8_out, B, not_2_out, D);
  and and_9 (and_9_out, not_1_out, not_3_out);
  and and_10 (and_10_out, C, not_3_out);
  and and_11 (and_11_out, not_2_out, not_3_out);
  and and_12 (and_12_out, B, not_2_out);
  and and_13 (and_13_out, B, not_3_out);
  and and_14 (and_14_out, B, not_2_out);
  and and_15 (and_15_out, not_1_out, C);
  and and_16 (and_16_out, C, not_3_out);
  or or_1 (a_2, A, and_1_out, C, and_2_out);
  or or_2 (b_2, not_1_out, and_3_out, and_4_out);
  or or_3 (c_2, B, not_2_out, D);
  or or_4 (d_2, A, and_5_out, and_6_out, and_7_out, and_8_out);
  or or_5 (e, and_9_out, and_10_out);
  or or_6 (f, A, and_11_out, and_12_out, and_13_out);
  or or_7 (g, A, and_14_out, and_15_out, and_16_out);
endmodule

module Decodificador2 (
  input  _0,
  input  _1,
  input  _2,
  input  _3,
  input  _0_2,
  input  _1_2,
  input  _2_2,
  input  _3_2,
  output out_9,
  output out_10,
  output out_11,
  output out_12,
  output b,
  output b_2,
  output b_3,
  output b_4
);

  wire and_1_out, not_1_out, not_2_out, not_3_out, not_4_out, not_5_out, not_6_out, not_7_out, not_8_out;

  not not_1 (not_1_out, _1);
  not not_2 (not_2_out, _2);
  not not_3 (not_3_out, _3);
  not not_4 (not_4_out, _0);
  not not_5 (not_5_out, _0_2);
  not not_6 (not_6_out, _1_2);
  not not_7 (not_7_out, _2_2);
  not not_8 (not_8_out, _3_2);
  and and_1 (and_1_out, not_4_out, not_1_out, not_2_out, not_3_out, not_8_out, not_7_out, not_6_out, not_5_out);
  Multiplexer #(.width(4), .enable("false")) multiplexer_1 (
    .in0({_3, _2, _1, _0}), .in1(4'b0001), .out({out_9, out_10, out_11, out_12}), .sel(and_1_out));
  Multiplexer #(.width(4), .enable("false")) multiplexer_2 (
    .in0({_3_2, _2_2, _1_2, _0_2}), .in1(4'b0100), .out({b_4, b_3, b_2, b}), .sel(and_1_out));
endmodule

module AUP (
  input  in_1,
  output out_2,
  output out_3,
  output out_4,
  output out_5,
  output out_6,
  output out_7,
  output out_8
);

  not not_1 (out_8, in_1);
  not not_2 (out_7, 1'b1);

  assign out_2 = 1'b1;
  assign out_3 = 1'b1;
  assign out_4 = 1'b1;
  assign out_5 = 1'b1;
  assign out_6 = 1'b1;
endmodule
